# Fritzing sketch FourDigital (saved by Fritzing 0.9.3b)
breadboards: 1

parts:
  Componente1 = Arduino Uno (Rev3)
  U1 = 7-SEGMENT-4DIGIT [package=7-segment-4digit-youngsun]
  R2 = Rotary Potentiometer (Large) [maximum_resistance=10kΩ package=THT]
  R3 = Rotary Potentiometer (Large) [maximum_resistance=10kΩ package=THT]
  R5 = Resistor [tolerance=±5% resistance=220 package=THT]
  R6 = Resistor [tolerance=±5% resistance=220 package=THT]
  R7 = Resistor [tolerance=±5% resistance=220 package=THT]
  R8 = Resistor [tolerance=±5% resistance=220 package=THT]

nets:
  N1: Componente1.A0, R2.wiper
  N2: Componente1.A1, R3.wiper
  N3: Componente1.D8, U1.14
  N4: Componente1.D9_PWM, U1.1
  N5: Componente1.D10_PWM/SS, U1.2
  N6: Componente1.D11_PWM/MOSI, U1.4
  N7: Componente1.D12/MISO, U1.9
  N8: Componente1.D13/SCK, U1.15
  N9: Componente1.D2, R5.Pin_1
  N10: Componente1.D3_PWM, R6.Pin_1
  N11: Componente1.D4, R7.Pin_1
  N12: Componente1.D5_PWM, R8.Pin_1
  N13: Componente1.D6_PWM, U1.3
  N14: Componente1.D7, U1.5
  N15: Componente1.5V, R2.leg2, R3.leg2
  N16: Componente1.GND, R2.leg1, R3.leg1
  N17: U1.6, R8.Pin_0
  N18: U1.11, R7.Pin_0
  N19: U1.13, R6.Pin_0
  N20: U1.16, R5.Pin_0
